# Fritzing sketch SingingPumpkinsProto (saved by Fritzing 0.7.10b)
stripboards: 1

parts:
  PWM1 = PCA9685 16x12-bit PWM Breakout
  Arduino1 = Arduino
  J1 = Basic Servo
  J2 = Basic Servo
  U1_PT5101 = Voltage Regulator - 5V [package="TO220 [THT]"]
  U2_PT5101 = Voltage Regulator - 5V [package="TO220 [THT]"]
  C1_2_2uF = Electrolytic Capacitor [capacitance=2.2µF voltage=50V package="100 mil [THT, electrolytic]"]
  C2_2_2uF = Electrolytic Capacitor [capacitance=2.2µF voltage=50V package="100 mil [THT, electrolytic]"]
  C3_100uF = Electrolytic Capacitor [capacitance=1mF voltage=10V package="200 mil [THT, electrolytic]"]
  C4_100uF = Electrolytic Capacitor [capacitance=1mF voltage=10V package="200 mil [THT, electrolytic]"]
  J3 = Screw terminal - 2 pins [package=THT]  # not connected
  LED1 = LED - 5mm [color="Blue (470nm)" package="5 mm [THT]"]

nets:
  N1: PWM1.no_name_yet#0, J1.pulse
  N2: PWM1.no_name_yet#2, J2.pulse
  N3: PWM1.no_name_yet#7, LED1.cathode
  N4: PWM1.no_name_yet#100, PWM1.no_name_yet#102, PWM1.no_name_yet#107, PWM1.no_name_yet#706, U2_PT5101.output_voltage, C4_100uF.+, LED1.anode
  GND: PWM1.no_name_yet#601, PWM1.no_name_yet#701, PWM1.no_name_yet#1000, PWM1.no_name_yet#1002, Arduino1.GND, U1_PT5101.GND, U2_PT5101.GND, C1_2_2uF.-, C2_2_2uF.-, C3_100uF.-, C4_100uF.-
  N5: PWM1.no_name_yet#603, Arduino1.A5
  N6: PWM1.no_name_yet#604, Arduino1.A4
  N7: PWM1.no_name_yet#605, Arduino1.+5V, U1_PT5101.output_voltage, C3_100uF.+
  N8: U1_PT5101.input_voltage, U2_PT5101.input_voltage, C1_2_2uF.+, C2_2_2uF.+

notes:
  12V DC Input
  Green Wire is Minus
  (I used a car battery)
  The little pumpkin servos are omitted for brevity. They are attached on the even numbered outputs in the same way as Michael and Vincent.
  Similarly for the LEDs on the odd outputs.
  Michael
  Vincent
  The WaveShield is not shown but is plugged atop the Arduino in the normal way. The headphone output of the WaveShield is connected to an amplifier with speakers.
  The PT5105's were salvaged switchers but have the same pin-out as a 7805. You should probably use a 7805 w/ a heatsink.
